# Fritzing sketch lab4_breadboard-schematic (saved by Fritzing 1.0.1rc)
breadboards: 1

parts:
  Raspberry_Pi_Sense_Hat1 = Raspberry Pi Sense Hat
  R1 = Resistor [tolerance=±5% power=0.25 resistance=220 package=THT]
  S1 = Pushbutton [package="[THT]"]

nets:
  3V3: Raspberry_Pi_Sense_Hat1.3v3, Raspberry_Pi_Sense_Hat1.3V3, R1.Pin_1
  N1: Raspberry_Pi_Sense_Hat1.GPIO3, R1.Pin_0, S1.Pin_1, S1.Pin_2
  N2: Raspberry_Pi_Sense_Hat1.GND, S1.Pin_3, S1.Pin_4

custom parts:
  Raspberry Pi Sense Hat: The Sense HAT is an add-on board for Raspberry Pi, made especially for the Astro Pi mission – it launched to the International Space Station in December 2015. The Sense HAT has an 8×8 RGB LED matrix, a five-button joystick and includes the following sensors: Gyroscope Accelerometer Magnetometer Temperature Barometric pressure Humidity
