# Fritzing sketch lab4_own_breadboard (saved by Fritzing 1.0.1rc)
breadboards: 1

parts:
  Part1 = Audio Jack Breakout

nets:
  N1: Part1.GND, Part1.RING_SHUNT, Part1.RING, Part1.TIP_SHUNT, Part1.TIP
